// Logisim project modelo_logisim.circ as structural Verilog: 1 circuit, main circuit main
module main (
  input  [2:0] in_1,
  input  [4:0] in_2
);

  wire [1:0] PCSrc;
  wire [31:0] address_predicted, bit_extender_1_out, bit_extender_2_out, br32_1_p3, br32_1_p4, dir_salto_ID,
       IR_ID_q, multiplexer_1_out, PC4, PC4_ID, register_1_q, rom_1_data;

  Multiplexer #(.select(2), .width(32), .disabled(0), .enable("false")) multiplexer_1 (
    .in0(PC4), .in1(address_predicted), .in2(PC4_ID), .in3(dir_salto_ID), .out(multiplexer_1_out), .sel(PCSrc));
  assign bit_extender_1_out = {{29{1'b0}}, in_1};  // Bit_Extender bit_extender_1
  Register #(.width(32)) register_1 (.D(multiplexer_1_out), .Q(register_1_q));  // open: en, clk, clr
  Adder #(.width(32)) adder_1 (.a(bit_extender_1_out), .b(register_1_q), .out(PC4));  // open: cin, cout
  ROM #(.addrWidth(16), .dataWidth(32)) rom_1 (.addr(register_1_q[15:0]), .data(rom_1_data));  // open: sel
  Register #(.width(32)) u_PC4_ID (.D(PC4), .Q(PC4_ID));  // open: en, clk, clr
  Register #(.width(32)) IR_ID (.D(rom_1_data), .Q(IR_ID_q));  // open: en, clk, clr
  Register #(.width(32)) address_predicted_ID ();  // open: D, en, Q, clk, clr
  assign bit_extender_2_out = {{17{1'b0}}, {IR_ID_q[15:11], IR_ID_q[9:0]}};  // Bit_Extender bit_extender_2
  Shifter #(.width(32)) shifter_1 (.in(bit_extender_2_out), .\dist (in_2), .out(dir_salto_ID));
  // BR32 br32_1: pin names not known; wires that end beside it: {IR_ID_q[25:21], IR_ID_q[10]}, IR_ID_q[20:16], br32_1_p3, br32_1_p4
  Comparator #(.width(32)) comparator_1 (.a(br32_1_p3), .b(br32_1_p4));  // open: gt, eq, lt
  Register #(.width(32)) Ctrl_EX ();  // open: D, en, Q, clk, clr
  Register #(.width(32)) BUSA_Ex (.D(br32_1_p3));  // open: en, Q, clk, clr
  Register #(.width(32)) BUSB_Ex (.D(br32_1_p4));  // open: en, Q, clk, clr
  Register #(.width(32)) InmExt_Ex (.D(bit_extender_2_out));  // open: en, Q, clk, clr
endmodule
